# Fritzing sketch circuit (saved by Fritzing 0.9.3b)
breadboards: 1

parts:
  WeMos_D1_R1 = WeMos D1 R2
  SERVO1 = Tower Pro SG90 servo [part_number=101246]
  SERVO2 = Tower Pro SG90 servo [part_number=101246]
  SERVO3 = Tower Pro SG90 servo [part_number=101246]

nets:
  N1: WeMos_D1_R1.(D5), SERVO1.Signal
  N2: WeMos_D1_R1.(D6), SERVO3.Signal
  N3: WeMos_D1_R1.(D7), SERVO2.Signal
  GND: WeMos_D1_R1.GND, SERVO1.GND, SERVO2.GND, SERVO3.GND
  +5V: WeMos_D1_R1.5V, SERVO1.+5V, SERVO2.+5V, SERVO3.+5V

custom parts:
  WeMos D1 R2: The D1 R2 is a mini wifi board based on the ESP-8266EX.
  Tower Pro SG90 servo: Original file by John De Cristofaro http://www.adafruit.com/products/1449 Adafruit Feedback Servo (Small) Edited by: e-radionica.com 28/9/2015
